# Fritzing sketch DSC_Full (saved by Fritzing 0.9.3b)
breadboards: 1

parts:
  Part1 = ACS712 Low Current Sensor Board v12
  Part2 = ACS712 Low Current Sensor Board v12
  Part3 = Adafruit AD8495 [part_number="Adafruit #1778"]
  Part4 = Adafruit AD8495 [part_number="Adafruit #1778"]
  Part5 = Adafruit Feather M0 Express [part_number="Adafruit #3403"]
  D1 = Rectifier Diode [part_number=1N4001 package="300 mil [THT]"]
  R3 = Resistor [tolerance=±1% resistance=5.1k package=THT]
  R4 = Resistor [tolerance=±1% resistance=5.1k package=THT]
  D3 = Rectifier Diode [part_number=1N4001 package="300 mil [THT]"]
  D2 = Rectifier Diode [part_number=1N4001 package="300 mil [THT]"]
  D6 = Rectifier Diode [part_number=1N4001 package="300 mil [THT]"]
  D7 = Rectifier Diode [part_number=1N4001 package="300 mil [THT]"]
  R6 = Resistor [tolerance=±1% resistance=10k package=THT]
  R5 = Resistor [tolerance=±1% resistance=10k package=THT]
  R8 = Resistor [tolerance=±1% resistance=10k package=THT]
  R9 = Resistor [tolerance=±1% resistance=10k package=THT]
  R10 = Resistor [tolerance=±5% resistance=48.7 power=400mW package=THT]
  R11 = Resistor [tolerance=±5% resistance=48.7 power=400mW package=THT]
  U1 = Transformer [package=transformer]
  U2 = Transformer [package=transformer]
  U3 = RELAY-SOLIDSTATE [package=relay-s108t02]
  U4 = RELAY-SOLIDSTATE [package=relay-s108t02]
  S1 = Toggle Switch [package=THT]
  S2 = Toggle Switch [package=THT]
  Fuse1 = Fuse with Handler [part_number=Htc-15m]
  Power_plug1 = Power plug

nets:
  N1: Part1.IP+, R10.Pin_1
  N2: Part1.IP-, U1.4
  5V: Part1.5V, Part2.5V, D1.cathode
  N3: Part1.VO, R3.Pin_0, R6.Pin_0
  GND: Part1.GND, Part2.GND, Part3.GND, Part4.GND, Part5.GND, D2.anode, D6.anode, R8.Pin_1, R9.Pin_1, U3.-, U4.-
  N4: Part2.IP+, R11.Pin_1
  N5: Part2.IP-, U2.4
  N6: Part2.VO, R4.Pin_1, R5.Pin_1
  VIN: Part3.VIN, Part4.VIN, Part5.+3V3, D3.cathode, D7.cathode
  N7: Part3.OUT, Part5.A1
  N8: Part4.OUT, Part5.A4
  N9: Part5.A3, R4.Pin_0, D6.cathode, D7.anode, R5.Pin_0, R8.Pin_0
  N10: Part5.A2, R3.Pin_1, D3.anode, D2.cathode, R6.Pin_1, R9.Pin_0
  N11: Part5.VBUS, D1.anode
  N12: Part5.D11, U3.+
  N13: Part5.D10, U4.+
  N14: R10.Pin_0, U1.3
  N15: R11.Pin_0, U2.3
  N16: U1.1, U3.T1
  N17: U1.2, U2.2, Fuse1.Connector2
  N18: U2.1, U4.T1
  N19: U3.T2, S1.L1
  N20: U4.T2, S2.L1
  N21: S1.COM, S2.COM, Power_plug1.GND
  N22: Fuse1.Connector1, Power_plug1.VCC

notes:
  Twisted pair, 24V AC
  Twisted pair, 120V AC

custom parts:
  Adafruit AD8495: Thermocouples are very sensitive, requiring a good amplifier with a cold-compensation reference. We have a couple digital thermocouple amplifiers in the shop already from Maxim. Now we're happy to introduce an excellent analog-output amplifier. This is a very simple sensor to use, and if your microcontroller has analog input capability, you'll be ready to go really fast! The AD8495 K-type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
  Adafruit Feather M0 Express: We love all our Feathers equally, but this Feather is very special. It's our first Feather that is specifically designed for use with CircuitPython! CircuitPython is our beginner-oriented flavor of MicroPython - and as the name hints at, its a small but full-featured version of the popular Python programming language specifically for use with circuitry and electronics. That doesn't mean you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
