# Fritzing sketch DSC_Sensors (saved by Fritzing 0.9.3b)
breadboards: 1

parts:
  Part1 = ACS712 Low Current Sensor Board v12
  Part2 = ACS712 Low Current Sensor Board v12
  Part3 = Adafruit AD8495 [part_number="Adafruit #1778"]
  Part4 = Adafruit AD8495 [part_number="Adafruit #1778"]
  Part5 = Adafruit Feather M0 Express [part_number="Adafruit #3403"]
  D1 = Rectifier Diode [part_number=1N4001 package="300 mil [THT]"]
  R3 = Resistor [tolerance=±1% resistance=5.1k package=THT]
  R4 = Resistor [tolerance=±1% resistance=5.1k package=THT]
  D3 = Rectifier Diode [part_number=1N4001 package="300 mil [THT]"]
  D2 = Rectifier Diode [part_number=1N4001 package="300 mil [THT]"]
  D6 = Rectifier Diode [part_number=1N4001 package="300 mil [THT]"]
  D7 = Rectifier Diode [part_number=1N4001 package="300 mil [THT]"]
  R6 = Resistor [tolerance=±1% resistance=10k package=THT]
  R5 = Resistor [tolerance=±1% resistance=10k package=THT]
  R8 = Resistor [tolerance=±1% resistance=10k package=THT]
  R9 = Resistor [tolerance=±1% resistance=10k package=THT]

nets:
  5V: Part1.5V, Part2.5V, D1.cathode
  N1: Part1.VO, R3.Pin_0, R6.Pin_0
  GND: Part1.GND, Part2.GND, Part3.GND, Part4.GND, Part5.GND, D2.anode, D6.anode, R8.Pin_1, R9.Pin_1
  N2: Part2.VO, R4.Pin_1, R5.Pin_1
  VIN: Part3.VIN, Part4.VIN, Part5.+3V3, D3.cathode, D7.cathode
  N3: Part3.OUT, Part5.A1
  N4: Part4.OUT, Part5.A4
  N5: Part5.A3, R4.Pin_0, D6.cathode, D7.anode, R5.Pin_0, R8.Pin_0
  N6: Part5.A2, R9.Pin_0
  N7: Part5.VBUS, D1.anode
  N8: R3.Pin_1, D3.anode, D2.cathode, R6.Pin_1

custom parts:
  Adafruit AD8495: Thermocouples are very sensitive, requiring a good amplifier with a cold-compensation reference. We have a couple digital thermocouple amplifiers in the shop already from Maxim. Now we're happy to introduce an excellent analog-output amplifier. This is a very simple sensor to use, and if your microcontroller has analog input capability, you'll be ready to go really fast! The AD8495 K-type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
  Adafruit Feather M0 Express: We love all our Feathers equally, but this Feather is very special. It's our first Feather that is specifically designed for use with CircuitPython! CircuitPython is our beginner-oriented flavor of MicroPython - and as the name hints at, its a small but full-featured version of the popular Python programming language specifically for use with circuitry and electronics. That doesn't mean you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
